# Fritzing sketch Sketch (saved by Fritzing 1.0.2b)
stripboards: 6

parts:
  Mod1 = ESP32 - CAM
  U1 = MPU 9250 Breakout [package="SIP (Single Inline) [THT]"]
  Part1 = BME280
  Part2 = BH1750
  ZS-042_RTC1 = ZS-042 RTC Module
  OLED1 = SSD1306 0.96in 128x64 I2C Monochrome OLED Display
  Part3 = Arduino Mega 2560 (Rev3)
  Part4 = RFID-RC522-v3
  A1 = Sim900a module
  RCWL-0516_Microwave_Radar_Motion_Sensor1 = RCWL-0516 Microwave Radar Motion Sensor Module
  SERVO1 = Tower Pro SG90 servo [part_number=101246]
  Grove1 = Grove Dust Sensor
  SM1 = 28BYJ-48 Stepper Motor [part_number=28BYJ-48]
  Driver1 = 28BYJ-48 Driver Module [part_number=ULN2003 package=THT]
  Part5 = HC-SR501 Body Sensor Module
  125_kHz_RFID_module1 = RDM6300
  Part6 = RDM6300-ANT
  A2 = NEO-6M GPS Module [part_number=GY-GPS6MV2]
  S1 = KY-026
  Part7 = INMP441  # not connected
  J1 = Piezo Speaker
  LED1 = RGB LED (com. cathode, rbg) [color="Red (633nm)" current=0.030A package="5 mm [THT]"]
  C1 = Electrolytic Capacitor [capacitance=100µF voltage=35V package="200 mil [THT, electrolytic]"]
  U3 = 2-Channel 5v Relay Shield [package=relay-2ch5v10a]
  Mod2 = MQ-7 breakout
  Mod3 = MQ-7 breakout
  Mod4 = MQ-7 breakout
  Mod5 = MQ-7 breakout
  Mod6 = MQ-7 breakout
  Mod7 = MQ-7 breakout
  Mod8 = MQ-7 breakout
  Mod9 = MQ-7 breakout
  Mod10 = MQ-7 breakout
  U2 = Voltage Regulator - 3.3V [package="TO220 [THT]"]
  J2 = Power Jack [package=power_jack_slot]

nets:
  GND: Mod1.GND, Mod1.IO12, Mod1.IO13, U1.GND, Part1.GND, Part2.GND, ZS-042_RTC1.GND, OLED1.GND, Part3.D17_PWM/RX2, Part3.GND, Part4.GND, A1.Pin_1, A1.Pin_8, RCWL-0516_Microwave_Radar_Motion_Sensor1.GND, SERVO1.GND, Grove1.GND, Driver1.GND, Part5.GND, 125_kHz_RFID_module1.TX, 125_kHz_RFID_module1.GND, A2.GND, S1.pin2, J1.pin1, LED1.common_cathode, C1.-, U3.GND, Mod2.GND, Mod3.GND, Mod4.GND, Mod5.GND, Mod6.GND, Mod7.GND, Mod8.GND, Mod9.GND, Mod10.GND, U2.GND, J2.GNDBREAK, J2.GND
  N1: Mod1.VOT, Part3.D0_RX0
  N2: Mod1.VOR, Part3.D1_TX0
  VCC: Mod1.VCC, Part3.VIN, A1.Pin_9, RCWL-0516_Microwave_Radar_Motion_Sensor1.VIN, SERVO1.+5V, Grove1.VCC, Driver1.Vmotor, Part5.VCC, 125_kHz_RFID_module1.+5V, A2.Vcc, S1.pin3, U3.VCC, Mod2.VCC, Mod3.VCC, Mod4.VCC, Mod5.VCC, Mod6.VCC, Mod7.VCC, Mod8.VCC, Mod9.VCC, Mod10.VCC, U2.input_voltage, J2.PWR
  VCC_2: U1.VCC, Part1.VIN, Part2.VCC, ZS-042_RTC1.VCC, OLED1.VCC, Part4.3.3V, C1.+, U2.output_voltage
  N3: U1.SCL, Part1.SCL, Part2.SCL, ZS-042_RTC1.SCL, OLED1.SCL, Part3.D21/SCL
  N4: U1.SDA, Part1.SDA, Part2.SDA, ZS-042_RTC1.SDA, OLED1.SDA, Part3.D20/SDA
  N5: ZS-042_RTC1.SQW, Part3.D2_PWM
  N6: Part3.A8, Mod4.AO
  N7: Part3.A9, S1.pin1
  N8: Part3.A0, Mod8.AO
  N9: Part3.A1, Mod2.AO
  N10: Part3.A2, Mod3.AO
  N11: Part3.A3, Mod5.AO
  N12: Part3.A4, Mod7.AO
  N13: Part3.A5, Mod6.AO
  N14: Part3.A6, Mod10.AO
  N15: Part3.A7, Mod9.AO
  N16: Part3.D19/RX1, A2.Tx
  N17: Part3.D18/TX1, A2.Rx
  N18: Part3.D16_PWM/TX2, 125_kHz_RFID_module1.RX
  N19: Part3.D15/RX3, A1.Pin_14
  N20: Part3.D14/TX3, A1.Pin_11
  N21: Part3.D11_PWM, J1.pin2
  N22: Part3.D10_PWM, LED1.red_anode
  N23: Part3.D9_PWM, LED1.blue_anode
  N24: Part3.D8_PWM, LED1.green_anode
  N25: Part3.D5_PWM, Part4.RST
  N26: Part3.D7_PWM, SERVO1.Signal
  N27: Part3.D23, U3.IN1
  N28: Part3.D25, U3.IN2
  N29: Part3.D28, Driver1.IN1
  N30: Part3.D30, Driver1.IN2
  N31: Part3.D32, Driver1.IN3
  N32: Part3.D34, Driver1.IN4
  N33: Part3.D36, RCWL-0516_Microwave_Radar_Motion_Sensor1.OUT
  N34: Part3.D37, Part5.OUT
  N35: Part3.D42, Grove1.NC
  N36: Part3.D43, Grove1.SIG
  N37: Part3.D50, Part4.MISO
  N38: Part3.D51, Part4.MOSI
  N39: Part3.D52, Part4.SCK
  N40: Part3.D53, Part4.SDA
  N41: SM1.blue-pin, Driver1.blue-pin
  N42: SM1.pink-pin, Driver1.pink-pin
  N43: SM1.yellow-pin, Driver1.yellow-pin
  N44: SM1.orange-pin, Driver1.orange-pin
  N45: SM1.red-pin, Driver1.red-pin
  N46: Driver1.ON/OFF-7, Driver1.ON/OFF-8
  N47: 125_kHz_RFID_module1.ANT1, Part6.ANT1
  N48: 125_kHz_RFID_module1.ANT2, Part6.ANT2

notes:
  Bitscoper IoT

custom parts:
  ESP32 - CAM: The ESP32-CAM has a very competitive small-size camera module that can operate independently as a minimum system with a footprint of only 27*40.5*4.5mm and a deep sleep current of up to 6mA.
  MPU 9250 Breakout: Generic MPU 9250 Breakout Board
  BH1750: Light Sensor
  RFID-RC522-v3: A simple China made RFID-RC522 Reader (6x4 cm); do check the pin labels, as this is a MFRC522 based clone.
  Sim900a module: SIM900A GSM module delivers GSM/GPRS 900/1800MHz performance for voice, SMS, Data, and Fax in a small form factor and with low power consumption.
  RCWL-0516 Microwave Radar Motion Sensor Module: The RCWL-0516 is a microwave radar motion sensor module. Input voltage is 4V to 28V. The 3V3 pin is a power output.
  Tower Pro SG90 servo: Original file by John De Cristofaro http://www.adafruit.com/products/1449 Adafruit Feedback Servo (Small) Edited by: e-radionica.com 28/9/2015
  Grove Dust Sensor: PPD42 Grove Dust Sensor
  28BYJ-48 Stepper Motor: Unipolar Stepper Motor 28BYJ-48 Top coil - pink & orange Bottom coil - blue & yellow Common rail - red Connector pins: blue - pink - yellow - orange - red
  28BYJ-48 Driver Module: High-power ULN2003 Stepper Motor Driver Board Test Module For Arduino AVR SMD
  HC-SR501 Body Sensor Module: Pyroelectric Infrared PIR Motion Sensor Detector Module
  RDM6300: 125 kHz RFID module (serial interface)
  RDM6300-ANT: Antenna
  NEO-6M GPS Module: GY-GPS6MV2 NEO-6M GPS Module Module based on U-blox NEO-6M GPS engine, incorporating regulator for 3.3-5V DC input, MS621FE-compatible rechargeable battery for backup and EEPROM for storing configuration settings. Links: NEO-6 series product information page NEO-6 Datasheet
  KY-026: ky-026 flame sensor module
  INMP441: This is a simple breakout board for the INMP441 I2S MEMS microphone.
  2-Channel 5v Relay Shield: 2 Channel 5v Relay Shield w. 2x SPD-06VDC-SD-C
  MQ-7 breakout: MQ-5 gas sensor
